# Fritzing sketch LED-Button (saved by Fritzing 1.0.2b)

parts:
  Mod1 = Raspberry Pi Pico W
  S3 = Round Pushbutton
  NEOPIXEL2 = Neopixel Strip -- White (30/m) [part_number=1376]

nets:
  N1: Mod1.pin_18, Mod1.pin_38, Mod1.pin_42, S3.leg0, NEOPIXEL2.GND
  N2: Mod1.pin_20, S3.leg1
  N3: Mod1.pin_34, NEOPIXEL2.Din
  N4: Mod1.pin_40, NEOPIXEL2.+5V

custom parts:
  Raspberry Pi Pico W: Raspberry Pi Pico W. Based around the RP2040 microcontroller the Pico W is a low cost microcontroller device bringing Raspberry Pi quality, cost, and easy of use to the microcontroller space. The areas marked KEEPOUT in pcb silkscreen should not have traces running through them to avoid shorts on a soldered in module!
  Neopixel Strip -- White (30/m): These NeoPixel strips have 30 digitally-addressable pixel LEDs per meter and are very affordable and are only 12.5 mm wide, 10 mm if you remove the strip from the casing.
